// Logisim project hw5_help.circ as structural Verilog
module MyXOR (
  input  X,
  input  X_2,
  output Z
);

  wire and_1_out, and_2_out, not_1_out, not_2_out;

  not not_1 (not_1_out, X);
  not not_2 (not_2_out, X_2);
  FullAdder fulladder_1 ();  // open: X, Y, CarryIn, sum, CarryOut
  and and_1 (and_1_out, not_1_out, X_2);
  and and_2 (and_2_out, X, not_2_out);
  or or_1 (Z, and_1_out, and_2_out);

  // Notes on the sheet:
  //   Here is a location to build an XOR circuit
  //   You can follow the tutorial (Help menu - "tutorial") or work on your own...
endmodule

module FullAdder (
  input  X,
  input  Y,
  input  CarryIn,
  output sum,
  output CarryOut
);

  wire and_1_out, and_2_out, and_3_out, and_4_out, and_5_out, and_6_out, and_7_out, and_8_out, not_1_out,
       not_2_out, not_3_out;

  not not_1 (not_1_out, X);
  not not_2 (not_2_out, Y);
  not not_3 (not_3_out, CarryIn);
  and and_1 (and_1_out, not_1_out, not_2_out, CarryIn);
  and and_2 (and_2_out, not_1_out, Y, not_3_out);
  and and_3 (and_3_out, X, not_2_out, not_3_out);
  and and_4 (and_4_out, X, Y, CarryIn);
  and and_5 (and_5_out, X, X, Y);
  and and_6 (and_6_out, X, Y, CarryIn);
  and and_7 (and_7_out, Y, CarryIn);
  and and_8 (and_8_out, CarryIn, X);
  or or_1 (sum, and_1_out, and_2_out, and_3_out, and_4_out);
  or or_2 (CarryOut, and_5_out, and_6_out, and_8_out, and_7_out);
endmodule

module _4_bit_Ripple_Carry_Adder (
  input  Y3,
  input  Y2,
  input  Y1,
  input  X3,
  input  X2,
  input  X1,
  input  X0,
  input  Y0,
  output Sum4,
  output Sum3,
  output Sum2,
  output Sum1,
  output Sum0
);

  wire fulladder_2_carryout, fulladder_3_carryout, fulladder_4_carryout;

  FullAdder fulladder_1 (.X(X3), .Y(Y3), .CarryIn(fulladder_2_carryout), .sum(Sum3), .CarryOut(Sum4));
  FullAdder fulladder_2 (.X(X2), .Y(Y2), .CarryIn(fulladder_3_carryout), .sum(Sum2), .CarryOut(fulladder_2_carryout));
  FullAdder fulladder_3 (.X(X1), .Y(Y1), .CarryIn(fulladder_4_carryout), .sum(Sum1), .CarryOut(fulladder_3_carryout));
  FullAdder fulladder_4 (.X(X0), .Y(Y0), .CarryIn(1'b0), .sum(Sum0), .CarryOut(fulladder_4_carryout));
endmodule

module _4_bit_Multiplier (
  input  Y3,
  input  Y2,
  input  Y1,
  input  Y0,
  input  X3,
  input  X2,
  input  X1,
  input  X0,
  output Z7,
  output Z6,
  output Z5,
  output Z4,
  output Z3,
  output Z2,
  output Z1,
  output Z0
);

  wire n4_bit_ripple_carry_adder_1_sum1, n4_bit_ripple_carry_adder_1_sum2, n4_bit_ripple_carry_adder_1_sum3,
       n4_bit_ripple_carry_adder_1_sum4, n4_bit_ripple_carry_adder_2_sum1, n4_bit_ripple_carry_adder_2_sum2,
       n4_bit_ripple_carry_adder_2_sum3, n4_bit_ripple_carry_adder_2_sum4, n4_by_1_multiplier_1_z_2,
       n4_by_1_multiplier_1_z_3, n4_by_1_multiplier_1_z_4, n4_by_1_multiplier_2_z, n4_by_1_multiplier_2_z_2,
       n4_by_1_multiplier_2_z_3, n4_by_1_multiplier_2_z_4, n4_by_1_multiplier_3_z, n4_by_1_multiplier_3_z_2,
       n4_by_1_multiplier_3_z_3, n4_by_1_multiplier_3_z_4, n4_by_1_multiplier_4_z, n4_by_1_multiplier_4_z_2,
       n4_by_1_multiplier_4_z_3, n4_by_1_multiplier_4_z_4;

  _4_by_1_Multiplier u_4_by_1_multiplier_1 (
    .Y3(Y3), .Y2(Y2), .Y1(Y1), .Y0(Y0), .X_n(X0), .Z(Z0), .Z_2(n4_by_1_multiplier_1_z_2),
    .Z_3(n4_by_1_multiplier_1_z_3), .Z_4(n4_by_1_multiplier_1_z_4));
  _4_by_1_Multiplier u_4_by_1_multiplier_2 (
    .Y3(Y3), .Y2(Y2), .Y1(Y1), .Y0(Y0), .X_n(X1), .Z(n4_by_1_multiplier_2_z), .Z_2(n4_by_1_multiplier_2_z_2),
    .Z_3(n4_by_1_multiplier_2_z_3), .Z_4(n4_by_1_multiplier_2_z_4));
  _4_by_1_Multiplier u_4_by_1_multiplier_3 (
    .Y3(Y3), .Y2(Y2), .Y1(Y1), .Y0(Y0), .X_n(X2), .Z(n4_by_1_multiplier_3_z), .Z_2(n4_by_1_multiplier_3_z_2),
    .Z_3(n4_by_1_multiplier_3_z_3), .Z_4(n4_by_1_multiplier_3_z_4));
  _4_by_1_Multiplier u_4_by_1_multiplier_4 (
    .Y3(Y3), .Y2(Y2), .Y1(Y1), .Y0(Y0), .X_n(X3), .Z(n4_by_1_multiplier_4_z), .Z_2(n4_by_1_multiplier_4_z_2),
    .Z_3(n4_by_1_multiplier_4_z_3), .Z_4(n4_by_1_multiplier_4_z_4));
  _4_bit_Ripple_Carry_Adder u_4_bit_ripple_carry_adder_1 (
    .Y3(n4_by_1_multiplier_2_z_4), .X3(1'b0), .Y2(n4_by_1_multiplier_2_z_3), .X2(n4_by_1_multiplier_1_z_4),
    .Y1(n4_by_1_multiplier_2_z_2), .X1(n4_by_1_multiplier_1_z_3), .X0(n4_by_1_multiplier_1_z_2),
    .Y0(n4_by_1_multiplier_2_z), .Sum4(n4_bit_ripple_carry_adder_1_sum4),
    .Sum3(n4_bit_ripple_carry_adder_1_sum3), .Sum2(n4_bit_ripple_carry_adder_1_sum2),
    .Sum1(n4_bit_ripple_carry_adder_1_sum1), .Sum0(Z1));
  _4_bit_Ripple_Carry_Adder u_4_bit_ripple_carry_adder_2 (
    .Y3(n4_by_1_multiplier_3_z_4), .X3(n4_bit_ripple_carry_adder_1_sum4), .Y2(n4_by_1_multiplier_3_z_3),
    .X2(n4_bit_ripple_carry_adder_1_sum3), .Y1(n4_by_1_multiplier_3_z_2),
    .X1(n4_bit_ripple_carry_adder_1_sum2), .X0(n4_bit_ripple_carry_adder_1_sum1),
    .Y0(n4_by_1_multiplier_3_z), .Sum4(n4_bit_ripple_carry_adder_2_sum4),
    .Sum3(n4_bit_ripple_carry_adder_2_sum3), .Sum2(n4_bit_ripple_carry_adder_2_sum2),
    .Sum1(n4_bit_ripple_carry_adder_2_sum1), .Sum0(Z2));
  _4_bit_Ripple_Carry_Adder u_4_bit_ripple_carry_adder_3 (
    .Y3(n4_by_1_multiplier_4_z_4), .X3(n4_bit_ripple_carry_adder_2_sum4), .Y2(n4_by_1_multiplier_4_z_3),
    .X2(n4_bit_ripple_carry_adder_2_sum3), .Y1(n4_by_1_multiplier_4_z_2),
    .X1(n4_bit_ripple_carry_adder_2_sum2), .X0(n4_bit_ripple_carry_adder_2_sum1),
    .Y0(n4_by_1_multiplier_4_z), .Sum4(Z7), .Sum3(Z6), .Sum2(Z5), .Sum1(Z4), .Sum0(Z3));

  // Notes on the sheet:
  //   factor (4 bits)
  //   See the problem for details on this hint: perhaps build a 4x1-bit multiplier first!
  //   second factor (4 bits)
  //   product (8 bits)
  //   most significant (highest) bit
  //   least significant (lowest) bit
endmodule

module _3by2_divider (
  input  Y2,
  input  Y1,
  input  Y0,
  input  X1,
  input  X0,
  output Z2,
  output Z1,
  output Z0
);

  wire and_1_out, and_2_out, and_3_out, and_4_out, and_5_out, and_6_out, and_7_out, and_8_out, and_9_out,
       and_10_out, and_11_out, and_12_out, and_13_out, and_14_out, and_15_out, and_16_out, and_17_out,
       and_18_out, and_19_out, and_20_out, and_21_out, and_22_out, and_23_out, and_24_out, and_25_out,
       not_1_out, not_2_out, not_3_out, not_4_out, not_5_out;

  not not_1 (not_1_out, Y2);
  not not_2 (not_2_out, Y1);
  not not_3 (not_3_out, Y0);
  not not_4 (not_4_out, X1);
  not not_5 (not_5_out, X0);
  and and_1 (and_1_out, Y2, not_2_out, not_3_out, not_4_out, X0);
  and and_2 (and_2_out, Y2, not_2_out, Y0, not_4_out, X0);
  and and_3 (and_3_out, Y2, Y1, not_3_out, not_4_out, X0);
  and and_4 (and_4_out, Y2, Y1, Y0, not_4_out, X0);
  and and_5 (and_5_out, not_1_out, Y1, not_3_out, not_4_out, X0);
  and and_6 (and_6_out, not_1_out, Y1, Y0, not_4_out, X0);
  and and_7 (and_7_out, Y2, Y1, not_3_out, not_4_out, X0);
  and and_8 (and_8_out, Y2, Y1, Y0, not_4_out, X0);
  and and_9 (and_9_out, Y2, not_2_out, not_3_out, X1, not_5_out);
  and and_10 (and_10_out, Y2, not_2_out, Y0, X1, not_5_out);
  and and_11 (and_11_out, Y2, Y1, not_3_out, X1, not_5_out);
  and and_12 (and_12_out, Y2, Y1, Y0, X1, not_5_out);
  and and_13 (and_13_out, Y2, Y1, not_3_out, X1, X0);
  and and_14 (and_14_out, Y2, Y1, Y0, X1, X0);
  and and_15 (and_15_out, not_1_out, not_2_out, Y0, not_4_out, X0);
  and and_16 (and_16_out, not_1_out, Y1, Y0, not_4_out, X0);
  and and_17 (and_17_out, Y2, not_2_out, Y0, not_4_out, X0);
  and and_18 (and_18_out, Y2, Y1, Y0, not_4_out, X0);
  and and_19 (and_19_out, not_1_out, Y1, not_3_out, X1, not_5_out);
  and and_20 (and_20_out, not_1_out, Y1, Y0, X1, not_5_out);
  and and_21 (and_21_out, Y2, Y1, not_3_out, X1, not_5_out);
  and and_22 (and_22_out, Y2, Y1, Y0, X1, not_5_out);
  and and_23 (and_23_out, not_1_out, Y1, Y0, X1, X0);
  and and_24 (and_24_out, Y2, not_2_out, not_3_out, X1, X0);
  and and_25 (and_25_out, Y2, not_2_out, Y0, X1, X0);
  // OR_Gate or_1 has open pins: in1=X1, in2=X0, out=open
  or or_2 (Z2, and_1_out, and_2_out, and_3_out, and_4_out);
  or or_3 (Z1, and_5_out, and_6_out, and_7_out, and_8_out, and_9_out, and_10_out, and_11_out, and_12_out, and_13_out, and_14_out);
  or or_4 (Z0, and_15_out, and_16_out, and_17_out, and_18_out, and_19_out, and_20_out, and_21_out, and_22_out, and_23_out, and_24_out, and_25_out);

  // Notes on the sheet:
  //   Dividend (3 bits: Y2 Y1 Y0)
  //   Divisor (2 bits: X1 X0)
endmodule

module _4_by_1_Multiplier (
  input  Y3,
  input  Y2,
  input  Y1,
  input  Y0,
  input  X_n,
  output Z,
  output Z_2,
  output Z_3,
  output Z_4
);

  and and_1 (Z, X_n, Y0);
  and and_2 (Z_2, X_n, Y1);
  and and_3 (Z_3, X_n, Y2);
  and and_4 (Z_4, X_n, Y3);

  // Notes on the sheet:
  //   3
endmodule
