// Logisim project hw5evolution.circ as structural Verilog: 10 circuits, main circuit MyXOR
module MyXOR (
  input  in_1,
  input  in_2,
  output out_3
);

  wire and_1_out, and_2_out, not_1_out, not_2_out;

  not not_1 (not_1_out, in_1);
  not not_2 (not_2_out, in_2);
  and and_1 (and_1_out, not_1_out, in_2);
  and and_2 (and_2_out, in_1, not_2_out);
  or or_1 (out_3, and_1_out, and_2_out);

  // Notes on the sheet:
  //   Here is a location to build an XOR circuit
  //   You can follow the tutorial (Help menu - "tutorial") or work on your own...
  //   XOR Circuit built using Logism
endmodule

module FullAdder (
  input  X,
  input  Y,
  input  CarryIn,
  output Sum,
  output CarryOut
);

  wire and_1_out, and_2_out, and_3_out, and_4_out, and_5_out, and_6_out, and_7_out, and_8_out, not_1_out,
       not_2_out, not_3_out;

  not not_1 (not_1_out, X);
  not not_2 (not_2_out, Y);
  not not_3 (not_3_out, CarryIn);
  and and_1 (and_1_out, not_1_out, not_1_out, not_2_out, CarryIn);
  and and_2 (and_2_out, not_1_out, Y, not_3_out, not_3_out);
  and and_3 (and_3_out, X, not_2_out, not_3_out);
  and and_4 (and_4_out, X, Y, CarryIn);
  and and_5 (and_5_out, not_1_out, Y, CarryIn);
  and and_6 (and_6_out, X, not_2_out, CarryIn);
  and and_7 (and_7_out, X, Y, Y, not_3_out);
  and and_8 (and_8_out, X, Y, CarryIn);
  or or_1 (Sum, and_1_out, and_2_out, and_3_out, and_4_out);
  or or_2 (CarryOut, and_5_out, and_6_out, and_7_out, and_8_out);

  // Notes on the sheet:
  //   3 input bits:  X,  Y,  and CarryIn
  //   Here is a location to build an FULL ADDER circuit
  //   (1) draw the other four rails   (2) you'll need 8 AND gates    (3)  you'll need 2 OR gates
  //   two output bits:  Sum and CarryOut
endmodule

module A_4bit_Ripple_Carry_Adder (
  input  Y3,
  input  Y2,
  input  Y1,
  input  Y0,
  input  X3,
  input  X2,
  input  X1,
  input  X0,
  output Sum4,
  output Sum3,
  output Sum2,
  output Sum1,
  output Sum0
);

  wire fulladder_2_carryout, fulladder_3_carryout, fulladder_4_carryout;

  FullAdder fulladder_1 (.X(X3), .Y(Y3), .CarryIn(fulladder_2_carryout), .Sum(Sum3), .CarryOut(Sum4));
  FullAdder fulladder_2 (.X(X2), .Y(Y2), .CarryIn(fulladder_3_carryout), .Sum(Sum2), .CarryOut(fulladder_2_carryout));
  FullAdder fulladder_3 (.X(X1), .Y(Y1), .CarryIn(fulladder_4_carryout), .Sum(Sum1), .CarryOut(fulladder_3_carryout));
  FullAdder fulladder_4 (.X(X0), .Y(Y0), .CarryIn(1'b0), .Sum(Sum0), .CarryOut(fulladder_4_carryout));

  // Notes on the sheet:
  //   Here is a location to build an 4-bit RIPPLE-CARRY ADDER circuit
  //   8 input bits
  //   5 output bits
endmodule

module A_4bit_Multiplier (
  input  Y3,
  input  Y2,
  input  Y1,
  input  Y0,
  input  X0,
  input  X1,
  input  X2,
  input  X3,
  output Z7,
  output Z6,
  output Z5,
  output Z4,
  output Z3,
  output Z2,
  output Z1,
  output Z0
);

  wire a_4bit_ripple_carry_adder_1_sum1, a_4bit_ripple_carry_adder_1_sum2, a_4bit_ripple_carry_adder_1_sum3,
       a_4bit_ripple_carry_adder_1_sum4, a_4bit_ripple_carry_adder_2_sum1, a_4bit_ripple_carry_adder_2_sum2,
       a_4bit_ripple_carry_adder_2_sum3, a_4bit_ripple_carry_adder_2_sum4, a_4x1_multiplier_1_z1,
       a_4x1_multiplier_1_z2, a_4x1_multiplier_1_z3, a_4x1_multiplier_2_z0, a_4x1_multiplier_2_z1,
       a_4x1_multiplier_2_z2, a_4x1_multiplier_2_z3, a_4x1_multiplier_3_z0, a_4x1_multiplier_3_z1,
       a_4x1_multiplier_3_z2, a_4x1_multiplier_3_z3, a_4x1_multiplier_4_z0, a_4x1_multiplier_4_z1,
       a_4x1_multiplier_4_z2, a_4x1_multiplier_4_z3;

  A_4x1_multiplier a_4x1_multiplier_1 (
    .X(X0), .Y3(Y3), .Y2(Y2), .Y1(Y1), .Y0(Y0), .Z3(a_4x1_multiplier_1_z3), .Z2(a_4x1_multiplier_1_z2),
    .Z1(a_4x1_multiplier_1_z1), .Z0(Z0));
  A_4x1_multiplier a_4x1_multiplier_2 (
    .X(X1), .Y3(Y3), .Y2(Y2), .Y1(Y1), .Y0(Y0), .Z3(a_4x1_multiplier_2_z3), .Z2(a_4x1_multiplier_2_z2),
    .Z1(a_4x1_multiplier_2_z1), .Z0(a_4x1_multiplier_2_z0));
  A_4x1_multiplier a_4x1_multiplier_3 (
    .X(X2), .Y3(Y3), .Y2(Y2), .Y1(Y1), .Y0(Y0), .Z3(a_4x1_multiplier_3_z3), .Z2(a_4x1_multiplier_3_z2),
    .Z1(a_4x1_multiplier_3_z1), .Z0(a_4x1_multiplier_3_z0));
  A_4x1_multiplier a_4x1_multiplier_4 (
    .X(X3), .Y3(Y3), .Y2(Y2), .Y1(Y1), .Y0(Y0), .Z3(a_4x1_multiplier_4_z3), .Z2(a_4x1_multiplier_4_z2),
    .Z1(a_4x1_multiplier_4_z1), .Z0(a_4x1_multiplier_4_z0));
  A_4bit_Ripple_Carry_Adder a_4bit_ripple_carry_adder_1 (
    .Y3(1'b0), .Y2(a_4x1_multiplier_1_z3), .Y1(a_4x1_multiplier_1_z2), .Y0(a_4x1_multiplier_1_z1),
    .X3(a_4x1_multiplier_2_z3), .X2(a_4x1_multiplier_2_z2), .X1(a_4x1_multiplier_2_z1),
    .X0(a_4x1_multiplier_2_z0), .Sum4(a_4bit_ripple_carry_adder_1_sum4),
    .Sum3(a_4bit_ripple_carry_adder_1_sum3), .Sum2(a_4bit_ripple_carry_adder_1_sum2),
    .Sum1(a_4bit_ripple_carry_adder_1_sum1), .Sum0(Z1));
  A_4bit_Ripple_Carry_Adder a_4bit_ripple_carry_adder_2 (
    .Y3(a_4bit_ripple_carry_adder_1_sum4), .Y2(a_4bit_ripple_carry_adder_1_sum3),
    .Y1(a_4bit_ripple_carry_adder_1_sum2), .Y0(a_4bit_ripple_carry_adder_1_sum1), .X3(a_4x1_multiplier_3_z3),
    .X2(a_4x1_multiplier_3_z2), .X1(a_4x1_multiplier_3_z1), .X0(a_4x1_multiplier_3_z0),
    .Sum4(a_4bit_ripple_carry_adder_2_sum4), .Sum3(a_4bit_ripple_carry_adder_2_sum3),
    .Sum2(a_4bit_ripple_carry_adder_2_sum2), .Sum1(a_4bit_ripple_carry_adder_2_sum1), .Sum0(Z2));
  A_4bit_Ripple_Carry_Adder a_4bit_ripple_carry_adder_3 (
    .Y3(a_4bit_ripple_carry_adder_2_sum4), .Y2(a_4bit_ripple_carry_adder_2_sum3),
    .Y1(a_4bit_ripple_carry_adder_2_sum2), .Y0(a_4bit_ripple_carry_adder_2_sum1), .X3(a_4x1_multiplier_4_z3),
    .X2(a_4x1_multiplier_4_z2), .X1(a_4x1_multiplier_4_z1), .X0(a_4x1_multiplier_4_z0), .Sum4(Z7), .Sum3(Z6),
    .Sum2(Z5), .Sum1(Z4), .Sum0(Z3));

  // Notes on the sheet:
  //   factor (4 bits)
  //   second factor (4 bits)
  //   See the problem for details on this hint:   Build a 4x1-bit multiplier first!
  //   4-bit MULTIPLIER circuit
  //   most significant (highest) output bit
  //   product (8 bits)
  //   least significant (lowest) output bit
endmodule

module A_3by2_divider (
  input  Y2,
  input  Y1,
  input  Y0,
  input  X1,
  input  X0,
  output Z2,
  output Z1,
  output Z0,
  output Error
);

  wire and_1_out, and_2_out, and_3_out, and_4_out, and_5_out, and_6_out, and_7_out, and_8_out, and_9_out,
       not_1_out, not_2_out, not_3_out, not_4_out, not_5_out, not_6_out, not_7_out, not_8_out, or_1_out;

  and and_1 (and_1_out, Y0, Y1, not_1_out);
  not not_1 (not_1_out, Y2);
  not not_2 (not_2_out, X1);
  not not_3 (not_3_out, X1);
  not not_4 (not_4_out, X0);
  not not_5 (not_5_out, X1);
  not not_6 (not_6_out, X0);
  not not_7 (not_7_out, Y1);
  not not_8 (not_8_out, Y1);
  or or_1 (or_1_out, X0, X1);
  and and_2 (and_2_out, X0, Y2, not_2_out);
  and and_3 (and_3_out, Y1, X0, X1, Y2);
  and and_4 (and_4_out, X0, Y1, not_3_out);
  and and_5 (and_5_out, not_4_out, X1, Y2);
  and and_6 (and_6_out, X0, Y0, not_5_out);
  and and_7 (and_7_out, not_6_out, X1, Y1);
  and and_8 (and_8_out, X0, Y0, not_7_out, Y2, X1);
  and and_9 (and_9_out, X0, not_8_out, Y2, X1);
  not not_9 (Error, or_1_out);
  buf or_2 (Z2, and_2_out);  // OR_Gate
  or or_3 (Z1, and_3_out, and_4_out, and_5_out);
  or or_4 (Z0, and_1_out, and_9_out, and_6_out, and_8_out, and_7_out);

  // Notes on the sheet:
  //   Dividend (3 bits: Y2 Y1 Y0)
  //   Divisor (2 bits: X1 X0)
  //   Quotient (4 bits: Z2 Z1 Z0 and Error)
  //   3-by-2-bit DIVIDER circuit
endmodule

module A_2bit_decoder (
  input  Input1,
  input  Input0,
  output Output0,
  output Output1,
  output Output2,
  output Output3
);

  wire not_1_out, not_2_out, or_1_out;

  not not_1 (not_1_out, Input1);
  not not_2 (not_2_out, Input0);
  or or_1 (or_1_out, Input1, Input0);
  not not_3 (Output0, or_1_out);
  and and_1 (Output1, Input0, not_1_out);
  and and_2 (Output2, not_2_out, Input1);
  and and_3 (Output3, Input0, Input1);

  // Notes on the sheet:
  //   2-bit DECODER circuit (extra credit - see hw)
endmodule

module A_12nGb_memory (
  input  X2,
  input  X1,
  input  X0,
  input  Input1,
  input  Input0,
  input  W,
  input  R,
  output Ouput2,
  output Ouput0,
  output Output1
);

  wire a_2bit_decoder_1_output0, a_2bit_decoder_1_output1, a_2bit_decoder_1_output2,
       a_2bit_decoder_1_output3, and_1_out, and_2_out, and_3_out, and_4_out, and_5_out, and_6_out, and_7_out,
       flip_flop_1_out_3, flip_flop_2_out_3, flip_flop_3_out_3, flip_flop_4_out_3, flip_flop_5_out_3,
       flip_flop_6_out_3, flip_flop_7_out_3, flip_flop_8_out_3, flip_flop_9_out_3, flip_flop_10_out_3,
       flip_flop_11_out_3, flip_flop_12_out_3;

  A_2bit_decoder a_2bit_decoder_1 (
    .Input1(Input1), .Input0(Input0), .Output0(a_2bit_decoder_1_output0), .Output1(a_2bit_decoder_1_output1),
    .Output2(a_2bit_decoder_1_output2), .Output3(a_2bit_decoder_1_output3));
  and and_1 (and_1_out, W, a_2bit_decoder_1_output0);
  and and_2 (and_2_out, a_2bit_decoder_1_output1, W);
  and and_3 (and_3_out, a_2bit_decoder_1_output1, R, a_2bit_decoder_1_output2, W);
  and and_4 (and_4_out, a_2bit_decoder_1_output1, R, a_2bit_decoder_1_output3, W);
  Flip_flop flip_flop_1 (.D(X2), .S(and_1_out), .out_3(flip_flop_1_out_3));
  Flip_flop flip_flop_2 (.D(X2), .S(and_2_out), .out_3(flip_flop_2_out_3));
  Flip_flop flip_flop_3 (.D(X2), .S(and_3_out), .out_3(flip_flop_3_out_3));
  Flip_flop flip_flop_4 (.D(X2), .S(and_4_out), .out_3(flip_flop_4_out_3));
  buf and_5 (and_5_out, flip_flop_1_out_3);  // AND_Gate
  and and_6 (and_6_out, flip_flop_4_out_3, flip_flop_3_out_3);
  or or_1 (Ouput0, and_6_out, and_5_out);
  Flip_flop flip_flop_5 (.D(X1), .S(and_1_out), .out_3(flip_flop_5_out_3));
  Flip_flop flip_flop_6 (.D(X1), .S(and_2_out), .out_3(flip_flop_6_out_3));
  Flip_flop flip_flop_7 (.D(X1), .S(X1), .out_3(flip_flop_7_out_3));
  Flip_flop flip_flop_8 (.D(X1), .S(and_4_out), .out_3(flip_flop_8_out_3));
  // OR_Gate or_2 has open pins: out=Output1
  Flip_flop flip_flop_9 (.D(X0), .S(and_4_out), .out_3(flip_flop_9_out_3));
  Flip_flop flip_flop_10 (.D(X0), .S(and_1_out), .out_3(flip_flop_10_out_3));
  Flip_flop flip_flop_11 (.D(X0), .S(and_2_out), .out_3(flip_flop_11_out_3));
  Flip_flop flip_flop_12 (.D(X0), .S(and_3_out), .out_3(flip_flop_12_out_3));
  and and_7 (and_7_out, and_4_out, flip_flop_11_out_3);
  or or_3 (Ouput2, and_7_out, flip_flop_10_out_3);

  // Notes on the sheet:
  //   12 nanogigabit MEMORY circuit (extra credit - see hw)
endmodule

module A_4x1_multiplier (
  input  X,
  input  Y3,
  input  Y2,
  input  Y1,
  input  Y0,
  output Z3,
  output Z2,
  output Z1,
  output Z0
);

  and and_1 (Z3, Y3, X);
  and and_2 (Z2, Y2, X);
  and and_3 (Z1, Y1, X);
  and and_4 (Z0, Y0, X);
endmodule

module SR_Latch (
  input  Set,
  input  Reset,
  output Q
);

  wire nor_1_out;

  nor nor_1 (nor_1_out, Set, Q);
  nor nor_2 (Q, nor_1_out, Reset);
endmodule

module Flip_flop (
  input  D,
  input  S,
  output out_3
);

  wire and_1_out, and_2_out, not_1_out;

  and and_1 (and_1_out, D, S);
  not not_1 (not_1_out, D);
  and and_2 (and_2_out, not_1_out, S);
  SR_Latch sr_latch_1 (.Set(and_1_out), .Reset(and_2_out), .Q(out_3));
endmodule
